# Fritzing sketch projectSketch (saved by Fritzing 0.9.6b)
breadboards: 1

parts:
  U1 = NodeMCU V1.0
  Mod1 = KY-026 Flame Sensor Module [package="Breakout board"]
  Mod2 = KY-013 Analog Temperature Sensor Module [package="Breakout board"]
  Mod3 = KY-012 Active Buzzer Module [package="Breakout board"]
  Mod4 = KY-032 IR Obstacle Avoidance Sensor Module [package="Breakout board"]

nets:
  N1: U1.D1, Mod4.out
  N2: U1.D2, Mod1.D0
  N3: U1.D3, Mod3.NC
  3V3: U1.3V3, Mod1.+, Mod2.Vin, Mod3.S, Mod4.+
  GND: U1.GND, Mod1.G, Mod2.-, Mod3.-, Mod4.GND
  N4: U1.A0, Mod2.S

custom parts:
  NodeMCU V1.0: ESP8266 based NodeMCU
  KY-026 Flame Sensor Module: KY-026 Flame Sensor Module reacts in the presence of fire.
  KY-013 Analog Temperature Sensor Module: KY-013 Analog Temperature Sensor module, measures ambient temperature based on resistance of the thermistor.
  KY-012 Active Buzzer Module: Active Piezoelectric Buzzer Module KY-012, it produces single-tone sound when signal is high. (Special thanks to vanepp for fixing the PCB holes and other errors)
  KY-032 IR Obstacle Avoidance Sensor Module: KY-032 Infrared Obstacle Avoidance Sensor. Distance-adjustable, infrared proximity sensor designed for wheeled robots. Also known as AD-032.
